// Logisim project SumOfFactors.circ as structural Verilog: 1 circuit, main circuit main
module main (
  input  [4:0] INPUT,
  output out_2,
  output out_3,
  output out_4,
  output out_5,
  output out_6,
  output out_7,
  output [5:0] out_8,
  output out_9,
  output out_10,
  output out_11,
  output out_12,
  output out_13,
  output [5:0] out_14
);

  wire and_1_out, and_2_out, and_3_out, and_4_out, and_5_out, and_6_out, and_7_out, and_8_out, and_9_out,
       and_10_out, and_11_out, and_12_out, and_13_out, and_14_out, and_15_out, and_16_out, and_17_out,
       and_18_out, and_19_out, and_20_out, and_21_out, and_22_out, and_23_out, and_24_out, and_25_out,
       and_26_out, and_27_out, and_28_out, and_29_out, and_30_out, and_31_out, and_32_out, and_33_out,
       and_34_out, and_35_out, and_36_out, and_37_out, and_38_out, and_39_out, and_40_out, and_41_out,
       and_42_out, and_43_out, and_44_out, and_45_out, and_46_out, and_47_out, and_48_out, and_49_out,
       and_50_out, and_51_out;

  and and_1 (and_1_out, INPUT[4], INPUT[3], INPUT[1], INPUT[0]);
  and and_2 (and_2_out, INPUT[4], INPUT[2], ~INPUT[1], ~INPUT[0]);  // AND_Gate
  or or_1 (out_2, and_1_out, and_4_out);
  and and_3 (and_3_out, INPUT[4], INPUT[3], ~INPUT[1], ~INPUT[0]);  // AND_Gate
  or or_2 (out_9, and_2_out, and_3_out, and_5_out);
  and and_4 (and_4_out, INPUT[4], ~INPUT[3], INPUT[2], ~INPUT[1], INPUT[0]);  // AND_Gate
  and and_5 (and_5_out, INPUT[4], INPUT[3], INPUT[2], ~INPUT[0]);  // AND_Gate
  and and_6 (and_6_out, INPUT[4], ~INPUT[3], ~INPUT[2], INPUT[0]);  // AND_Gate
  and and_7 (and_7_out, INPUT[3], INPUT[2], ~INPUT[0]);  // AND_Gate
  and and_8 (and_8_out, INPUT[4], ~INPUT[3], INPUT[1], INPUT[0]);  // AND_Gate
  and and_9 (and_9_out, INPUT[4], INPUT[3], ~INPUT[1], INPUT[0]);  // AND_Gate
  or or_3 (out_3, and_6_out, and_8_out, and_9_out, and_11_out, and_13_out);
  and and_10 (and_10_out, INPUT[4], ~INPUT[2], ~INPUT[0]);  // AND_Gate
  or or_4 (out_10, and_7_out, and_10_out, and_12_out);
  and and_11 (and_11_out, ~INPUT[4], INPUT[3], INPUT[2], INPUT[1], INPUT[0]);  // AND_Gate
  and and_12 (and_12_out, INPUT[4], INPUT[1], ~INPUT[0]);  // AND_Gate
  and and_13 (and_13_out, INPUT[4], INPUT[3], INPUT[2], INPUT[1], ~INPUT[0]);  // AND_Gate
  and and_14 (and_14_out, INPUT[3], ~INPUT[2], ~INPUT[0]);  // AND_Gate
  and and_15 (and_15_out, ~INPUT[4], INPUT[3], INPUT[0]);  // AND_Gate
  and and_16 (and_16_out, ~INPUT[3], INPUT[2], INPUT[1], ~INPUT[0]);  // AND_Gate
  or or_5 (out_11, and_14_out, and_16_out, and_18_out, and_20_out);
  and and_17 (and_17_out, INPUT[3], ~INPUT[2], INPUT[0]);  // AND_Gate
  and and_18 (and_18_out, INPUT[4], ~INPUT[2], ~INPUT[0]);  // AND_Gate
  and and_19 (and_19_out, INPUT[4], INPUT[1], ~INPUT[0]);  // AND_Gate
  and and_20 (and_20_out, INPUT[4], ~INPUT[3], INPUT[1], ~INPUT[0]);  // AND_Gate
  and and_21 (and_21_out, ~INPUT[3], INPUT[2], INPUT[1], INPUT[0]);  // AND_Gate
  or or_6 (out_4, and_15_out, and_17_out, and_19_out, and_21_out, and_23_out, and_25_out);
  and and_22 (and_22_out, ~INPUT[3], INPUT[2], ~INPUT[1], ~INPUT[0]);  // AND_Gate
  and and_23 (and_23_out, ~INPUT[4], INPUT[3], INPUT[2], INPUT[1]);  // AND_Gate
  and and_24 (and_24_out, ~INPUT[4], INPUT[3], ~INPUT[2], ~INPUT[0]);  // AND_Gate
  or or_7 (out_12, and_22_out, and_24_out, and_26_out, and_28_out);
  and and_25 (and_25_out, INPUT[4], INPUT[3], INPUT[2], ~INPUT[1]);  // AND_Gate
  and and_26 (and_26_out, INPUT[3], ~INPUT[2], INPUT[1], ~INPUT[0]);  // AND_Gate
  and and_27 (and_27_out, INPUT[3], ~INPUT[1], INPUT[0]);  // AND_Gate
  and and_28 (and_28_out, INPUT[4], ~INPUT[3], ~INPUT[1], ~INPUT[0]);  // AND_Gate
  and and_29 (and_29_out, ~INPUT[4], ~INPUT[2], INPUT[1], INPUT[0]);  // AND_Gate
  and and_30 (and_30_out, ~INPUT[3], ~INPUT[2], INPUT[1], ~INPUT[0]);  // AND_Gate
  and and_31 (and_31_out, ~INPUT[4], INPUT[2], ~INPUT[1], INPUT[0]);  // AND_Gate
  and and_32 (and_32_out, ~INPUT[3], INPUT[2], INPUT[1], ~INPUT[0]);  // AND_Gate
  and and_33 (and_33_out, INPUT[4], ~INPUT[3], ~INPUT[2], ~INPUT[0]);  // AND_Gate
  or or_8 (out_13, and_30_out, and_33_out, and_35_out, and_37_out);
  and and_34 (and_34_out, INPUT[3], ~INPUT[2], INPUT[1], ~INPUT[0]);  // AND_Gate
  or or_9 (out_5, and_27_out, and_29_out, and_31_out, and_32_out, and_34_out, and_36_out, and_38_out, and_39_out, and_40_out);
  and and_35 (and_35_out, ~INPUT[4], ~INPUT[3], INPUT[2], ~INPUT[1], ~INPUT[0]);  // AND_Gate
  and and_36 (and_36_out, ~INPUT[4], INPUT[3], INPUT[2], ~INPUT[1]);  // AND_Gate
  and and_37 (and_37_out, ~INPUT[4], INPUT[3], ~INPUT[2], ~INPUT[1], ~INPUT[0]);  // AND_Gate
  and and_38 (and_38_out, INPUT[4], ~INPUT[3], ~INPUT[2], INPUT[1]);  // AND_Gate
  and and_39 (and_39_out, INPUT[4], ~INPUT[3], INPUT[2], ~INPUT[0]);  // AND_Gate
  and and_40 (and_40_out, INPUT[4], INPUT[3], ~INPUT[2], ~INPUT[1]);  // AND_Gate
  and and_41 (and_41_out, ~INPUT[4], INPUT[2], ~INPUT[1], INPUT[0]);  // AND_Gate
  and and_42 (and_42_out, INPUT[3], ~INPUT[2], INPUT[1], ~INPUT[0]);  // AND_Gate
  and and_43 (and_43_out, INPUT[3], INPUT[2], ~INPUT[1], INPUT[0]);  // AND_Gate
  or or_10 (out_6, and_41_out, and_42_out, and_43_out, and_45_out, and_44_out);
  and and_44 (and_44_out, INPUT[4], ~INPUT[3], INPUT[2], ~INPUT[1], ~INPUT[0]);  // AND_Gate
  and and_45 (and_45_out, INPUT[4], ~INPUT[2], ~INPUT[1], INPUT[0]);  // AND_Gate
  and and_46 (and_46_out, ~INPUT[3], ~INPUT[2], INPUT[1], ~INPUT[0]);  // AND_Gate
  and and_47 (and_47_out, ~INPUT[4], ~INPUT[2], ~INPUT[1], INPUT[0]);  // AND_Gate
  and and_48 (and_48_out, ~INPUT[4], INPUT[3], ~INPUT[2], ~INPUT[1]);  // AND_Gate
  and and_49 (and_49_out, INPUT[3], ~INPUT[2], ~INPUT[1], INPUT[0]);  // AND_Gate
  or or_11 (out_7, and_47_out, and_46_out, and_48_out, and_49_out, and_50_out, and_51_out);
  and and_50 (and_50_out, INPUT[4], ~INPUT[3], ~INPUT[2], ~INPUT[0]);  // AND_Gate
  and and_51 (and_51_out, ~INPUT[4], ~INPUT[3], INPUT[2], ~INPUT[1], ~INPUT[0]);  // AND_Gate

  assign out_8 = {out_2, out_3, out_4, out_5, out_6, out_7};
  assign out_14 = {out_9, out_10, out_11, out_12, out_13, 1'b0};

  // Notes on the sheet:
  //   SUM OF ODD FACTORS
  //   SUM OF EVEN FACTORS
endmodule
